# Fritzing sketch vaihe5 (saved by Fritzing 0.9.4)
breadboards: 1

parts:
  Part1 = Photon
  DHT1 = Humidity and Temperature Sensor DHT11
  R1 = Resistor [tolerance=±5% resistance=1k package=THT]

nets:
  N1: Part1.GND, DHT1.GND_2
  N2: Part1.D0, DHT1.Data-signal, R1.Pin_1
  3V3: Part1.3V3, DHT1.Vcc, R1.Pin_0

custom parts:
  Humidity and Temperature Sensor DHT11: Digital relative humidity & temperature sensor DHT11
